// Digital circuit 4BitAdder.dig as structural Verilog
module _4BitAdder (
  input  [3:0] A,
  input  [3:0] B,
  input  CI,
  output [3:0] O,
  output CO
);

  wire fulladder_1_c, fulladder_2_c, fulladder_3_c;

  FullAdder fulladder_1 (.CI(CI), .A(A[0]), .B(B[0]), .O(O[0]), .C(fulladder_1_c));
  FullAdder fulladder_2 (.CI(fulladder_1_c), .A(A[1]), .B(B[1]), .O(O[1]), .C(fulladder_2_c));
  FullAdder fulladder_3 (.CI(fulladder_2_c), .A(A[2]), .B(B[2]), .O(O[2]), .C(fulladder_3_c));
  FullAdder fulladder_4 (.CI(fulladder_3_c), .A(A[3]), .B(B[3]), .O(O[3]), .C(CO));
endmodule
