// Digital circuit 4BitAdderSubtractor.dig as structural Verilog
module _4BitAdderSubtractor (
  input  Subtract_flag,
  input  [3:0] A,
  input  [3:0] B,
  output [3:0] O,
  output CO
);

  wire [3:0] onescomplement_1_o;

  OnesComplement onescomplement_1 (.I(B), .Invert_flag(Subtract_flag), .O(onescomplement_1_o));
  _4BitAdder _4bitadder_1 (.A(A), .B(onescomplement_1_o), .CI(Subtract_flag), .CO(CO));  // open: O
endmodule
