// Digital circuit 4BitFlipFlopCounter.dig as structural Verilog
module _4BitFlipFlopCounter (
  input  clk
);

  wire B0, B1, B2, B3, d_ff_as_1_nq, d_ff_as_2_nq, d_ff_as_3_nq, d_ff_as_4_nq, resetdata_1_o, resetdata_2_o,
       resetdata_3_o, resetdata_4_o, Rst;

  ResetData resetdata_1 (.D(d_ff_as_1_nq), .R(Rst), .O(resetdata_1_o));
  D_FF_AS d_ff_as_1 (.Set(1'b0), .D(resetdata_1_o), .C(d_ff_as_2_nq), .Clr(Rst), .Q(B3), .nQ(d_ff_as_1_nq));
  ResetData resetdata_2 (.D(d_ff_as_2_nq), .R(Rst), .O(resetdata_2_o));
  D_FF_AS d_ff_as_2 (.Set(1'b0), .D(resetdata_2_o), .C(d_ff_as_3_nq), .Clr(Rst), .Q(B2), .nQ(d_ff_as_2_nq));
  ResetData resetdata_3 (.D(d_ff_as_3_nq), .R(Rst), .O(resetdata_3_o));
  D_FF_AS d_ff_as_3 (.Set(1'b0), .D(resetdata_3_o), .C(d_ff_as_4_nq), .Clr(Rst), .Q(B1), .nQ(d_ff_as_3_nq));
  ResetData resetdata_4 (.D(d_ff_as_4_nq), .R(Rst), .O(resetdata_4_o));
  Seven_Seg_Hex seven_seg_hex_1 (.d({B3, B2, B1, B0}), .dp(1'b0));
  D_FF_AS d_ff_as_4 (.Set(1'b0), .D(resetdata_4_o), .C(clk), .Clr(Rst), .Q(B0), .nQ(d_ff_as_4_nq));
  Button button_1 (.out(Rst));
endmodule
