// Digital circuit FullAdder.dig as structural Verilog
module FullAdder (
  input  CI,
  input  A,
  input  B,
  output O,
  output C
);

  wire halfadder_1_c, halfadder_1_o, halfadder_2_c;

  HalfAdder halfadder_1 (.I1(A), .I2(B), .O(halfadder_1_o), .C(halfadder_1_c));
  HalfAdder halfadder_2 (.I1(CI), .I2(halfadder_1_o), .O(O), .C(halfadder_2_c));
  or or_1 (C, halfadder_2_c, halfadder_1_c);
endmodule
