// Digital circuit OnesComplement.dig as structural Verilog
module OnesComplement (
  input  [3:0] I,
  input  Invert_flag,
  output [3:0] O
);

  xor xor_1 (O[0], I[0], Invert_flag);
  xor xor_2 (O[1], I[1], Invert_flag);
  xor xor_3 (O[2], I[2], Invert_flag);
  xor xor_4 (O[3], I[3], Invert_flag);
endmodule
