// Digital circuit ResetData.dig as structural Verilog
module ResetData (
  input  D,
  input  R,
  output O
);

  wire not_1_out;

  not not_1 (not_1_out, R);
  and and_1 (O, D, not_1_out);
endmodule
